# Fritzing sketch DesignProject1 (saved by Fritzing 0.9.3b)
breadboards: 1

parts:
  Raspberry_Pi_1 = Raspberry Pi 3 [part_number=RPI-3-V1.2]  # not connected
  Part1 = Adafruit T-Cobbler Plus [part_number="Adafruit #1989 and #2028"]
  IC1 = L293D [package=THT]  # not connected
  LED1 = smd LED [color="Green (565nm)" package="0603 [SMD]"]
  LED2 = smd LED [color="Yellow (592nm)" package="0603 [SMD]"]
  LED3 = smd LED [color="Red (633nm)" package="0603 [SMD]"]
  J1 = Basic Servo
  R1 = Resistor [tolerance=±5% resistance=220 package=THT]
  R2 = Resistor [tolerance=±5% resistance=220 package=THT]
  R3 = Resistor [tolerance=±5% resistance=220 package=THT]

nets:
  N1: Part1.+3.3V, R1.Pin_1, R2.Pin_1, R3.Pin_1
  GND: Part1.GND, J1.gnd
  N2: Part1.GPIO19, J1.pulse
  +5V: Part1.+5V, J1.vcc
  N3: Part1.GPIO16, LED1.anode
  N4: Part1.GPIO20, LED2.anode
  N5: Part1.GPIO21, LED3.anode
  N6: LED1.cathode, R2.Pin_0
  N7: LED2.cathode, R1.Pin_0
  N8: LED3.cathode, R3.Pin_0

custom parts:
  Adafruit T-Cobbler Plus: The Raspberry Pi has landed on the Maker World like a 40-GPIO pinned, quad-USB ported, credit card sized bomb of DIY joy. And while you can use most of our great Model B accessories by hooking up our downgrade cable, its probably a good time to upgrade your set up and accessorize using all of the 40 pins. That's why we now carry the Assembled Adafruit Pi T-Cobbler Plus - Breakout + Cable for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
